# Fritzing sketch Sketch (saved by Fritzing 0.9.3b)
perfboards: 1

parts:
  Espessif_Serial_Wifi_Modul_1 = ESP8266 ESP01 [part_number=ESP8266 package=THT]
  U1 = LIPO-1000mAh [package=lipo-1000]
  Bauteil1 = Si7021
  R1 = Resistor [tolerance=±5% resistance=3.3k package="2010 [SMD]"]
  R2 = Resistor [tolerance=±5% resistance=3.3k package="2010 [SMD]"]
  C1 = Capacitor Polarized [package=panasonic_g]

nets:
  GND: Espessif_Serial_Wifi_Modul_1.GND, U1.-, Bauteil1.GND, C1.-
  VCC: Espessif_Serial_Wifi_Modul_1.VCC, Espessif_Serial_Wifi_Modul_1.CH_PD, U1.+, Bauteil1.VCC, R1.Pin_0, R2.Pin_0, C1.+
  N1: Espessif_Serial_Wifi_Modul_1.GPIO00, Bauteil1.SCL, R1.Pin_1
  N2: Espessif_Serial_Wifi_Modul_1.GPIO02, Bauteil1.SDA, R2.Pin_1

custom parts:
  ESP8266 ESP01: Generic WiFi Module based on the ESP8266 with onboard PCB antenna and UART communications
  Si7021: Si7021 humidity and temperature sensor
